// Logisim project Preparacao_02.circ as structural Verilog: 1 circuit, main circuit main
module main (
  input  x,
  input  y,
  output S
);

  wire NOT_1_out, NOT_2_out, NOT_3_out, OR_1_out, OR_2_out;

  not NOT_1 (NOT_1_out, x);
  not NOT_2 (NOT_2_out, y);
  and OR_1 (OR_1_out, x, NOT_1_out);
  or OR_2 (OR_2_out, NOT_2_out, y);
  not NOT_3 (NOT_3_out, OR_2_out);
  and AND_1 (S, OR_1_out, NOT_3_out);
endmodule
