// Logisim project Preparacao_03.circ as structural Verilog: 2 circuits, main circuit mux
module mux (
  input  A,
  input  chave,
  input  B,
  output out_4
);

  wire AND_1_out, AND_2_out, NOT_1_out;

  not NOT_1 (NOT_1_out, chave);
  and AND_1 (AND_1_out, A, NOT_1_out);
  and AND_2 (AND_2_out, chave, B);
  or OR_1 (out_4, AND_1_out, AND_2_out);
endmodule

module a (
  input  a,
  input  b,
  input  c,
  output s
);

  wire not_1_out, not_2_out, not_3_out, saida1_out_4, saida2_out_4;

  not not_1 (not_1_out, b);
  not not_2 (not_2_out, a);
  mux saida1 (.A(a), .chave(c), .B(b), .out_4(saida1_out_4));
  not not_3 (not_3_out, c);
  mux saida2 (.A(not_1_out), .chave(c), .B(not_2_out), .out_4(saida2_out_4));
  mux \final  (.A(saida1_out_4), .chave(not_3_out), .B(saida2_out_4), .out_4(s));
endmodule
