// Logisim project Preparacao_05.circ as structural Verilog: 1 circuit, main circuit main
module main (
  input  a,
  input  b,
  output out_3
);

  wire nor_1_out, not_a_out, not_b_out, xnor_1_out;

  not not_b (not_b_out, b);
  not not_a (not_a_out, a);
  xnor xnor_1 (xnor_1_out, a, b);
  nor nor_1 (nor_1_out, not_b_out, not_a_out);
  nand \nand  (out_3, xnor_1_out, nor_1_out);
endmodule
